# Fritzing sketch schematic (saved by Fritzing 0.9.3b)
breadboards: 1

parts:
  Raspberry_Pi1 = Raspberry Pi 3 [part_number=RPI-3-V1.2]
  Thermal_Camera = IC, DIP package, 6 pins [chip_label="IR Grid 3 Click"]
  Fan = mystery part, 3 pins [chip_label="Fan Module V1.0"]
  Relay = IC, DIP package, 6 pins [chip_label=SRD-05VDC]
  Buzzer = Buzzer 12mm [package=buzzer-ccv-kit]
  Transformer = mystery part, 2 pins [chip_label=U]

nets:
  3V3: Raspberry_Pi1.3v3, Raspberry_Pi1.3V3, Thermal_Camera.pin5
  N1: Raspberry_Pi1.GPIO2, Thermal_Camera.pin4
  N2: Raspberry_Pi1.GPIO3, Thermal_Camera.pin3
  N3: Raspberry_Pi1.GND, Thermal_Camera.pin1, Thermal_Camera.pin2, Fan.pin3, Relay.pin3, Buzzer.2
  N4: Raspberry_Pi1.GPIO13, Relay.pin2
  N5: Raspberry_Pi1.GPIO12, Fan.pin2
  N6: Raspberry_Pi1.GPIO23, Buzzer.1
  N7: Raspberry_Pi1.5V, Thermal_Camera.pin6, Fan.pin1, Relay.pin1
  N8: Relay.pin5, Transformer.pin2
  GND: Relay.pin6
  230V: Transformer.pin1
